# Fritzing sketch garageos-fritzing (saved by Fritzing 0.9.2b)
breadboards: 1

parts:
  Door_2_Wall_Switch = Pushbutton [package="[SMD]"]
  U4 = RELAY [package=relay-jzc]
  Car_Distance_Ping_Sensor = SRF05 Ultrasonic Rangefinder
  RGB_LED = RGB LED (com. cathode, rgb) [package="5 mm [THT]"]
  Part1 = Photon
  U3 = RELAY [package=relay-jzc]
  Door_1_Wall_Switch = Pushbutton [package="[SMD]"]
  Door_1_Reed_Switch = Reed switch [package=THT]
  Door_2_Reed_Switch = Reed switch [package=THT]

nets:
  N1: Door_2_Wall_Switch.Pin_1, Door_2_Wall_Switch.Pin_2, U3.COIL1
  N2: Door_2_Wall_Switch.Pin_3, Door_2_Wall_Switch.Pin_4, U3.MAIN
  N3: U4.COIL2, Part1.D0
  GND: U4.NO, Car_Distance_Ping_Sensor.GND, RGB_LED.common_cathode, Part1.GND, U3.NO, Door_1_Reed_Switch.pin_1, Door_2_Reed_Switch.pin_1
  N4: U4.MAIN, Door_1_Wall_Switch.Pin_3, Door_1_Wall_Switch.Pin_4
  N5: U4.COIL1, Door_1_Wall_Switch.Pin_1
  VCC: Car_Distance_Ping_Sensor.VCC, Part1.3V3
  N6: Car_Distance_Ping_Sensor.Trig, Part1.D6
  N7: Car_Distance_Ping_Sensor.Echo, Part1.D7
  N8: RGB_LED.red_anode, Part1.A3
  N9: RGB_LED.green_anode, Part1.A2
  N10: RGB_LED.blue_anode, Part1.A4
  N11: Part1.A0, Door_1_Reed_Switch.pin_2
  N12: Part1.A1, Door_2_Reed_Switch.pin_2
  N13: Part1.D1, U3.COIL2
